# Fritzing sketch OSAA SpaceApi (saved by Fritzing 0.9.2b)
circuit board: 8.46667cm x 5.64444cm

parts:
  Raspberry_Pi_B_rev2 = Raspberry Pi B rev2
  LED1 = LED - 5mm [color="Red (633nm)" package="5 mm [THT]"]
  R1 = Resistor [tolerance=±5% resistance=470 package=THT]
  LED2 = LED - 5mm [color="Green (555nm)" package="5 mm [THT]"]
  R2 = Resistor [tolerance=±5% resistance=470 package=THT]
  R3 = Resistor [tolerance=±5% resistance=1M package=THT]
  S1 = Round Pushbutton

nets:
  3.3V: Raspberry_Pi_B_rev2.3V3, R3.Pin_1
  5V: Raspberry_Pi_B_rev2.5V
  N1: Raspberry_Pi_B_rev2.GPIO_2, LED1.cathode
  N2: Raspberry_Pi_B_rev2.GPIO_3, LED2.cathode
  GND: Raspberry_Pi_B_rev2.GND, R1.Pin_1, R2.Pin_1, S1.leg0
  N3: Raspberry_Pi_B_rev2.GPIO_4, R3.Pin_0, S1.leg1
  N4: LED1.anode, R1.Pin_0
  N5: LED2.anode, R2.Pin_0
